# Fritzing sketch quickdraw_circuit (saved by Fritzing 0.9.3b)
breadboards: 1
perfboards: 1

parts:
  Raspberry_Pi_1 = Raspberry Pi 3 [part_number=RPI-3-V1.2]
  J20 = Camdenboss CTB0158-2 [part_number=CTB0158-2 package=THT]
  J21 = Camdenboss CTB0158-2 [part_number=CTB0158-2 package=THT]
  J23 = Camdenboss CTB0158-2 [part_number=CTB0158-2 package=THT]
  J24 = Camdenboss CTB0158-2 [part_number=CTB0158-2 package=THT]
  IC2 = MCP3008 8-channel 10-bit ADC [part_number=MCP3008]
  R21 = Resistor [tolerance=±5% resistance=1M package="2512 [SMD]"]
  J25 = Camdenboss CTB0158-2 [part_number=CTB0158-2 package=THT]
  J26 = Camdenboss CTB0158-2 [part_number=CTB0158-2 package=THT]
  J27 = Camdenboss CTB0158-2 [part_number=CTB0158-2 package=THT]
  J28 = Camdenboss CTB0158-2 [part_number=CTB0158-2 package=THT]
  Part1 = 24 NeoPixel Ring [part_number=1586]
  Part2 = Adafruit Micro USB Breakout [part_number="Adafruit #1833"]  # not connected
  J29 = Camdenboss CTB0158-4 [part_number=CTB0158-4 package=THT]
  J30 = Camdenboss CTB0158-4 [part_number=CTB0158-4 package=THT]
  Part5 = Adafruit Micro USB Breakout [part_number="Adafruit #1833"]  # not connected
  J31 = Camdenboss CTB0158-4 [part_number=CTB0158-4 package=THT]
  J32 = Camdenboss CTB0158-4 [part_number=CTB0158-4 package=THT]  # not connected
  J33 = Camdenboss CTB0158-4 [part_number=CTB0158-4 package=THT]
  Part6 = 24 NeoPixel Ring [part_number=1586]
  J34 = Camdenboss CTB0158-4 [part_number=CTB0158-4 package=THT]
  Part7 = 24 NeoPixel Ring [part_number=1586]
  J35 = Camdenboss CTB0158-4 [part_number=CTB0158-4 package=THT]
  Part8 = 24 NeoPixel Ring [part_number=1586]
  Part9 = 24 NeoPixel Ring [part_number=1586]
  Part10 = 24 NeoPixel Ring [part_number=1586]
  J36 = Camdenboss CTB0158-4 [part_number=CTB0158-4 package=THT]
  J37 = Camdenboss CTB0158-4 [part_number=CTB0158-4 package=THT]
  J38 = Camdenboss CTB0158-4 [part_number=CTB0158-4 package=THT]
  S1 = Toggle Switch [package=THT]  # not connected

nets:
  N1: Raspberry_Pi_1.GPIO21, J33.terminal_4
  N2: Raspberry_Pi_1.GPIO20, J37.terminal_4
  N3: Raspberry_Pi_1.GPIO25, IC2.no_name_yet#13
  N4: Raspberry_Pi_1.GPIO24, IC2.no_name_yet#12
  N5: Raspberry_Pi_1.GPIO23, IC2.no_name_yet#11
  N6: Raspberry_Pi_1.GPIO18, IC2.no_name_yet#10
  N7: Raspberry_Pi_1.GND, J20.pin1, J20.pin2, J21.pin1, J21.pin2, J23.pin1, J23.pin2, J24.pin1, J24.pin2, IC2.no_name_yet#9, IC2.no_name_yet#14, R21.Pin_0
  N8: Raspberry_Pi_1.5V, IC2.no_name_yet#15, IC2.no_name_yet#16
  N9: IC2.no_name_yet#1, J25.pin2
  N10: IC2.no_name_yet#2, J25.pin1
  N11: IC2.no_name_yet#3, J26.pin2
  N12: IC2.no_name_yet#4, J26.pin1
  N13: IC2.no_name_yet#5, J27.pin2
  N14: IC2.no_name_yet#6, J27.pin1
  N15: R21.Pin_1, J28.pin1
  N16: Part1.IN, J33.pin4
  N17: Part1.OUT, J33.pin1
  N18: Part1.VDD, J33.pin3
  N19: Part1.GND, J33.pin2
  N20: J29.terminal_1, J36.terminal_3, J37.terminal_3, J38.terminal_3
  N21: J30.pin4, J33.terminal_3, J34.terminal_3, J35.terminal_3
  N22: J31.terminal_1, J36.terminal_2, J37.terminal_2, J38.terminal_2
  N23: J33.terminal_1, J34.terminal_4
  N24: J33.terminal_2, J34.terminal_2, J35.terminal_2
  N25: Part6.IN, J34.pin4
  N26: Part6.OUT, J34.pin1
  N27: Part6.VDD, J34.pin3
  N28: Part6.GND, J34.pin2
  N29: J34.terminal_1, J35.terminal_4
  N30: Part7.IN, J35.pin4
  N31: Part7.OUT, J35.pin1
  N32: Part7.VDD, J35.pin3
  N33: Part7.GND, J35.pin2
  N34: Part8.IN, J36.pin4
  N35: Part8.OUT, J36.pin1
  N36: Part8.VDD, J36.pin3
  N37: Part8.GND, J36.pin2
  N38: Part9.IN, J37.pin4
  N39: Part9.OUT, J37.pin1
  N40: Part9.VDD, J37.pin3
  N41: Part9.GND, J37.pin2
  N42: Part10.IN, J38.pin4
  N43: Part10.OUT, J38.pin1
  N44: Part10.VDD, J38.pin3
  N45: Part10.GND, J38.pin2
  N46: J36.terminal_4, J38.terminal_1
  N47: J37.terminal_1, J38.terminal_4

custom parts:
  24 NeoPixel Ring: 24 ultra bright smart LED NeoPixels are arranged in a circle with 2.6" (66mm) outer diameter. The rings are 'chainable' - connect the output pin of one to the input pin of another. Use only one microcontroller pin to control as many as you can chain together! Each LED is addressable as the driver chip is inside the LED. Each one has ~18mA constant current drive so the color will be very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
  Adafruit Micro USB Breakout: Simple but effective - this breakout board has a USB Micro-B connector, with all 5 pins broken out. Great for pairing with a microcontroller with USB support, or adding USB 5V power to a project. We use a micro-AB connector with through-hole shielding pads for an excellent strong connection - it won't rip off by accident! Comes with one fully assembled and tested micro B breakout PCB and a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
